# Fritzing sketch ModuleRFIDNano (saved by Fritzing 0.9.3b)
perfboards: 1

parts:
  Composant1 = Arduino Nano (Rev3.0)
  LED1 = LED - 5mm [color="Red (633nm)" package="5 mm [THT]"]
  LED2 = LED - 5mm [color="Green (565nm)" package="5 mm [THT]"]
  LED3 = LED - 5mm [color="Blue (525nm)" package="5 mm [THT]"]
  Part3 = RFID-RC522-v2
  KY-2 = Keyes Relay [package=THT]

nets:
  GND: Composant1.GND, LED1.cathode, LED2.cathode, LED3.cathode, Part3.GND, KY-2.ground
  N1: Composant1.D4, KY-2.signal
  N2: Composant1.D5, LED1.anode
  N3: Composant1.D6, LED2.anode
  N4: Composant1.D8, LED3.anode
  N5: Composant1.D9, Part3.RST
  N6: Composant1.D10, Part3.SDA
  N7: Composant1.D11/MOSI, Part3.MOSI
  N8: Composant1.D12/MISO, Part3.MISO
  N9: Composant1.5V, KY-2.power
  3V3: Composant1.3V3, Part3.3.3V
  N10: Composant1.D13/SCK, Part3.SCK

custom parts:
  RFID-RC522-v2: A simple China made RFID-RC522 Reader; do check the pin labels, as this is a MFRC522 based clone.
  Keyes Relay: The Keyes 5V relay module is suitable for SCM development, home appliance control. It uses a 5V~12V TIL control signal which can control DC / AC signal.
